// Logisim project test_proc.circ as structural Verilog: 1 circuit, main circuit main
module main (
);

  wire cdm16_1_p1, mem, not_1_out, ram_1_p4, read, word;
  wire [15:0] address_bus, cdm16_1_p6, cdm16_1_p7, data_bus;

  // cdm16 cdm16_1: pin names not known; wires that end beside it: cdm16_1_p1, mem, read, word, address_bus, cdm16_1_p6, cdm16_1_p7
  Clock clock_1 (.out(cdm16_1_p1));
  assign data_bus = not_1_out ? cdm16_1_p6 : 16'bz;  // Controlled_Buffer controlled_buffer_1
  not not_1 (not_1_out, read);
  assign cdm16_1_p7 = read ? data_bus : 16'bz;  // Controlled_Buffer controlled_buffer_2
  // Debugger debugger_1: pin names not known
  // RAM ram_1: pin names not known; wires that end beside it: address_bus, word, mem, ram_1_p4, read, data_bus
  Clock clock_2 (.out(ram_1_p4));
endmodule
